# Fritzing sketch Solenoid (saved by Fritzing 0.9.3b)
breadboards: 1

parts:
  12V_in = male pin header, 1 pin [form="♂ (male)"]
  Vo_Atmega128 = Resistor [tolerance=±5% resistance=1k package="0603 [SMD]"]
  Vo = male pin header, 1 pin [form="♂ (male)"]
  D1 = Rectifier Diode [package="Melf DO-213 AA [SMD]"]
  Q1 = TRANSISTOR_NPN [package=to-92]

nets:
  12V: 12V_in.pin1
  N1: Vo_Atmega128.Pin_0, Q1.B
  N2: Vo_Atmega128.Pin_1, Vo.pin1
  N3: D1.cathode, Q1.E
  GND: D1.anode
  5V: Q1.C

notes:
  5V
  12V
  Solenoid, This is the circuit to control the solenoid and the motor., 1
