# Fritzing sketch breadboard (saved by Fritzing 0.9.3b)
breadboards: 4

parts:
  Microcontroller = IC, DIP package, 40 pins [chip_label="Atmega 162"]
  RESET = Pushbutton [package="[SMD]"]
  LED = LED - 3mm [color="Red (633nm)" package="3 mm [THT]"]
  VCC1 = Battery block 9V
  C3 = Capacitor [package=cap-pth-small]
  U1 = Voltage Regulator - 5V [package="TO220 [THT]"]
  Clock = Crystal [frequency="4 MHz" package=THT]
  RS232 = IC, DIP package, 20 pins [chip_label=MAX233]
  C4 = Capacitor [package=cap-pth-large]
  UART_connector = male pin header, 5 pins [form="♂ (male)"]
  CAN_controller = IC, DIP package, 18 pins [chip_label=MCP2515]
  C2 = Capacitor [package=cap-pth-large]
  CAN_trancv = IC, DIP package, 8 pins [chip_label=MC2551]
  Latch = IC, DIP package, 20 pins [chip_label=SN74ALS573C]
  C5 = Ceramic Capacitor [capacitance="100 nF" package="0603 [SMD, multilayer]"]
  ADC = DIP - 20 pins [chip_label=ADC0844CCN package="DIP (Dual Inline) [THT]"]
  SRAM = IC, DIP package, 28 pins [chip_label="SRAM IDT_7164SL"]
  C6 = Ceramic Capacitor [capacitance="100 nF" package="0603 [SMD, multilayer]"]
  GAL = IC, DIP package, 20 pins [chip_label=GAL16V8D]
  C7 = Ceramic Capacitor [capacitance="100 nF" package="0603 [SMD, multilayer]"]
  JTAG = male pin header, 4 pins [form="♂ (male)"]

nets:
  N1: Microcontroller.pin1, LED.anode
  N2: Microcontroller.pin9, RESET.Pin_1, RESET.Pin_2
  Rx: Microcontroller.pin10, RS232.pin3
  Tx: Microcontroller.pin11, RS232.pin2
  !WR: Microcontroller.pin16, ADC.!WR, SRAM.pin27
  !RD: Microcontroller.pin17, ADC.!RD, SRAM.pin22
  N3: Microcontroller.pin18, Clock.pin_1
  N4: Microcontroller.pin19, Clock.pin_0
  GND: Microcontroller.pin20, RESET.Pin_3, RESET.Pin_4, LED.cathode, VCC1.-, C3.2, U1.GND, RS232.pin6, C4.2, CAN_controller.pin9, C2.2, Latch.pin1, Latch.pin10, C5.1, ADC.AGND, ADC.DGND, SRAM.pin2, SRAM.pin14, GAL.pin10, C7.0
  A11: Microcontroller.pin21, SRAM.pin23, GAL.pin4
  A10: Microcontroller.pin22, SRAM.pin21, GAL.pin3
  A9: Microcontroller.pin23, SRAM.pin24, GAL.pin2
  A8: Microcontroller.pin24, SRAM.pin25, GAL.pin1
  JTAG4: Microcontroller.pin25, JTAG.pin1
  JTAG3: Microcontroller.pin26, JTAG.pin2
  JTAG2: Microcontroller.pin27, JTAG.pin3
  JTAG1: Microcontroller.pin28, JTAG.pin4
  LE: Microcontroller.pin30, Latch.pin11
  data7: Microcontroller.pin32, Latch.pin9, ADC.DB7, SRAM.pin19
  data6: Microcontroller.pin33, Latch.pin8, ADC.DB6, SRAM.pin18
  data5: Microcontroller.pin34, Latch.pin7, ADC.DB5, SRAM.pin17
  data4: Microcontroller.pin35, Latch.pin6, ADC.DB4, SRAM.pin16
  data3: Microcontroller.pin36, Latch.pin5, ADC.DB3, SRAM.pin15
  data2: Microcontroller.pin37, Latch.pin4, ADC.DB2, SRAM.pin13
  data1: Microcontroller.pin38, Latch.pin3, ADC.DB1, SRAM.pin12
  data0: Microcontroller.pin39, Latch.pin2, ADC.DB0, SRAM.pin11
  5V: Microcontroller.pin40, U1.output_voltage, RS232.pin7, C4.1, CAN_controller.pin18, C2.1, CAN_trancv.pin3, Latch.pin20, C5.0, ADC.VREF, ADC.VCC, SRAM.pin26, SRAM.pin28, C6.0, GAL.pin20, C7.1
  N5: VCC1.+, C3.1, U1.input_voltage
  R1IN: RS232.pin4, UART_connector.pin3
  T1OUT: RS232.pin5, UART_connector.pin4
  N6: RS232.pin10, RS232.pin16
  N7: RS232.pin11, RS232.pin15
  N8: RS232.pin12, RS232.pin17
  dataOut7: Latch.pin12, SRAM.pin3
  dataOut6: Latch.pin13, SRAM.pin4
  dataOut5: Latch.pin14, SRAM.pin5
  dataOut4: Latch.pin15, SRAM.pin6
  dataOut3: Latch.pin16, SRAM.pin7
  dataOut2: Latch.pin17, SRAM.pin8
  dataOut1: Latch.pin18, SRAM.pin9
  dataOut0: Latch.pin19, SRAM.pin10
  !CS_ADC: ADC.!CS, GAL.pin18
  !CS_SRAM: SRAM.pin20, GAL.pin19

notes:
  POWER SUPPLY, 1
  LATCH, 1
  UART - RS232, 1
  CAN BUS, 1
  ADC, 1
  JTAG
  RESET
  UART
  STATUS ON/OFF
  GND
  5V
  CS/WR
  Data/Addr
  TX/RX
  OLED/GPIO

custom parts:
  DIP - 20 pins: A DIP stand-in part for whatever IC you want. With 20 pins on a 300mil dual inline package (DIP) footprint.
